# Fritzing sketch Schaltplan GPS Uhr (saved by Fritzing 0.9.3b)

parts:
  Bauteil1 = Arduino Uno (Rev3)
  LCD1 = LCD screen
  MIC1 = Microphone

nets:
  N1: Bauteil1.D9_PWM, LCD1.DB4
  N2: Bauteil1.D10_PWM/SS, LCD1.DB5
  N3: Bauteil1.D11_PWM/MOSI, LCD1.DB6
  N4: Bauteil1.D12/MISO, LCD1.DB7
  N5: Bauteil1.D2, MIC1.pin1
  N6: Bauteil1.D3_PWM, LCD1.RS
  N7: Bauteil1.D5_PWM, LCD1.E
  5V: Bauteil1.5V, LCD1.VDD, LCD1.LED+
  N8: Bauteil1.GND, MIC1.pin2
  N9: LCD1.VSS, LCD1.R/W, LCD1.LED-

notes:
  1 2 3 4
  Schaltplan GPS Uhr
  K
  A
  D7
  D6
  D5
  D4
  D3
  D2
  D1
  D0
  E
  RW
  RS
  V0
  VDD
  VSS
